# Fritzing sketch schaltplan (saved by Fritzing 0.9.4)
breadboards: 2

parts:
  U1 = ESP32-38PinWide [part_number=ESP32-38PinWide]
  Bauteil1 = Real Time Clock Module - DS1307 RTC Breakout Board
  microSD1 = MicroSD Card Module
  U2 = LCD-16X2 [package=lcd-16x2_noholes]
  U3 = LCD-16X2 [package=lcd-16x2_noholes]
  LCM1602_IIC1 = LCM1602 IIC [part_number="LCM1602 IIC" chip_label="LCM1602 IIC" package="DIP (Dual Inline) [THT]"]
  LCM1602_IIC2 = LCM1602 IIC [part_number="LCM1602 IIC" chip_label="LCM1602 IIC" package="DIP (Dual Inline) [THT]"]
  Bauteil2 = Arduino Nano (Rev3.0)
  Bauteil3 = Arduino Nano (Rev3.0)
  Keypad4x1 = Keypad Membran 4x4
  Keypad4x2 = Keypad Membran 4x4
  J1 = Basic Servo
  J2 = Basic Servo
  R1 = Resistor [tolerance=±5% resistance=10k package="0603 [SMD]"]
  R2 = Resistor [tolerance=±5% resistance=10k package="0805 [SMD]"]
  HC-SR04_Sensor_1 = HC-SR04 Ultrasonic Distance Sensor
  HC-SR04_Sensor_2 = HC-SR04 Ultrasonic Distance Sensor

nets:
  GND: U1.GND, Bauteil1.GND, microSD1.GND, LCM1602_IIC1.GND, LCM1602_IIC2.GND, Bauteil2.GND, Bauteil3.GND, J1.gnd, J2.gnd, R1.Pin_1, R2.Pin_0, HC-SR04_Sensor_1.GND, HC-SR04_Sensor_2.GND
  VCC: U1.VIN, Bauteil1.5V, microSD1.VCC, LCM1602_IIC1.VCC, LCM1602_IIC2.VCC, Bauteil2.VIN, Bauteil3.VIN, J1.vcc, J2.vcc, HC-SR04_Sensor_1.VCC, HC-SR04_Sensor_2.VCC
  N1: U1.GPIO5, microSD1.CS
  N2: U1.GPIO18, microSD1.SCK
  N3: U1.GPIO19, microSD1.MISO
  N4: U1.GPIO21, Bauteil1.SDA, LCM1602_IIC1.SDA, LCM1602_IIC2.SDA, Bauteil2.A4, Bauteil3.A4
  N5: U1.GPIO22, Bauteil1.SCL, LCM1602_IIC1.SCL, LCM1602_IIC2.SCL, Bauteil2.A5, Bauteil3.A5
  N6: U1.GPIO23, microSD1.MOSI
  VSS: U2.VSS, LCM1602_IIC2.VSS
  VDD: U2.VDD, LCM1602_IIC2.VDD
  N7: U2.VO, LCM1602_IIC2.V0
  N8: U2.RS, LCM1602_IIC2.RS
  N9: U2.R_W, LCM1602_IIC2.RW
  N10: U2.E, LCM1602_IIC2.E
  N11: U2.DB0, LCM1602_IIC2.D0
  N12: U2.DB1, LCM1602_IIC2.D1
  N13: U2.DB2, LCM1602_IIC2.D2
  N14: U2.DB3, LCM1602_IIC2.D3
  N15: U2.DB4, LCM1602_IIC2.D4
  N16: U2.DB5, LCM1602_IIC2.D5
  N17: U2.DB6, LCM1602_IIC2.D6
  N18: U2.DB7, LCM1602_IIC2.D7
  N19: U2.A, LCM1602_IIC2.A
  N20: U2.K, LCM1602_IIC2.K
  VSS_2: U3.VSS, LCM1602_IIC1.VSS
  VDD_2: U3.VDD, LCM1602_IIC1.VDD
  N21: U3.VO, LCM1602_IIC1.V0
  N22: U3.RS, LCM1602_IIC1.RS
  N23: U3.R_W, LCM1602_IIC1.RW
  N24: U3.E, LCM1602_IIC1.E
  N25: U3.DB0, LCM1602_IIC1.D0
  N26: U3.DB1, LCM1602_IIC1.D1
  N27: U3.DB2, LCM1602_IIC1.D2
  N28: U3.DB3, LCM1602_IIC1.D3
  N29: U3.DB4, LCM1602_IIC1.D4
  N30: U3.DB5, LCM1602_IIC1.D5
  N31: U3.DB6, LCM1602_IIC1.D6
  N32: U3.DB7, LCM1602_IIC1.D7
  N33: U3.A, LCM1602_IIC1.A
  N34: U3.K, LCM1602_IIC1.K
  N35: Bauteil2.D2, Keypad4x1.Pin1
  N36: Bauteil2.D3, Keypad4x1.Pin2
  N37: Bauteil2.D4, Keypad4x1.Pin3
  N38: Bauteil2.D5, Keypad4x1.Pin4
  N39: Bauteil2.D6, Keypad4x1.Pin5
  N40: Bauteil2.D7, Keypad4x1.Pin6
  N41: Bauteil2.D8, Keypad4x1.Pin7
  N42: Bauteil2.D9, Keypad4x1.Pin8
  N43: Bauteil2.D10, HC-SR04_Sensor_2.TRIG
  N44: Bauteil2.D11/MOSI, HC-SR04_Sensor_2.ECHO
  N45: Bauteil2.D12/MISO, J1.pulse, R2.Pin_1
  N46: Bauteil3.D2, Keypad4x2.Pin1
  N47: Bauteil3.D3, Keypad4x2.Pin2
  N48: Bauteil3.D4, Keypad4x2.Pin3
  N49: Bauteil3.D5, Keypad4x2.Pin4
  N50: Bauteil3.D6, Keypad4x2.Pin5
  N51: Bauteil3.D7, Keypad4x2.Pin6
  N52: Bauteil3.D8, Keypad4x2.Pin7
  N53: Bauteil3.D9, Keypad4x2.Pin8
  N54: Bauteil3.D10, HC-SR04_Sensor_1.TRIG
  N55: Bauteil3.D11/MOSI, HC-SR04_Sensor_1.ECHO
  N56: Bauteil3.D12/MISO, J2.pulse, R1.Pin_0

custom parts:
  ESP32-38PinWide: Generic 38-Pin ESP32 with wide format (only access to one side of pins on a breadboard) based on Stephen Lilley's HiLetgo ESP-WROOM-32 ESP32 ESP-32S Development Board.
  LCM1602 IIC: I2C-Module to use a 1602 or 2004 LCD on with the wire.h libory Serial LCD Modul
  Keypad Membran 4x4: Membrane Keypad 4x4 Matrix
